# Fritzing sketch frighino (saved by Fritzing 0.9.3b)
breadboards: 1

parts:
  Componente1 = Arduino Uno (Rev3)
  T1 = LM35 Temperature Sensor [package="TO92 [THT]"]
  T2 = LM35 Temperature Sensor [package="TO92 [THT]"]
  T3 = LM35 Temperature Sensor [package="TO92 [THT]"]
  T4 = LM35 Temperature Sensor [package="TO92 [THT]"]
  R2 = Resistor [tolerance=±5% resistance=220 package="2512 [SMD]"]
  R3 = Resistor [tolerance=±5% resistance=220 package="2512 [SMD]"]
  R4 = Resistor [tolerance=±5% resistance=220 package="2512 [SMD]"]
  Q1 = MOSFET-NCHANNEL [package=to220v]
  Q2 = MOSFET-NCHANNEL [package=to220v]
  Q3 = MOSFET-NCHANNEL [package=to220v]
  U1 = RELAY [package=relay-t9a]
  R1 = Resistor [tolerance=±5% resistance=220 package="2512 [SMD]"]
  D1 = Diode [package=diode-1n4001]

nets:
  N1: Componente1.A0, T3.Vout
  N2: Componente1.A1, T2.Vout
  N3: Componente1.A2, T1.Vout
  N4: Componente1.A3, T4.Vout
  N5: Componente1.D9_PWM, Q2.G
  N6: Componente1.D10_PWM/SS, Q1.G
  N7: Componente1.D11_PWM/MOSI, Q3.G
  GND: T1.GND, T2.GND, T3.GND, T4.GND, U1.COIL1, D1.A
  N8: R2.Pin_0, R3.Pin_0, R4.Pin_1, R1.Pin_0
  N9: U1.COIL2, D1.C
